# Fritzing sketch PiBot (saved by Fritzing 0.9.2b)
breadboards: 1

parts:
  Raspberry_Pi1 = Raspberry Pi B+
  U1 = L298 [package=multiwatt15]
  Right_Front = DC Motor
  Right_Rear = DC Motor
  Left_Front = DC Motor
  Left_Rear = DC Motor
  J1 = Basic Servo
  Part1 = HC-SR04 Ultrasonic Rangemeter
  PIR1 = PIR sensor
  VCC1 = Battery

nets:
  N1: Raspberry_Pi1.GPIO4, PIR1.SIG
  GND: Raspberry_Pi1.GND, Part1.GND, PIR1.GND
  N2: Raspberry_Pi1.GPIO17, U1.ENA
  N3: Raspberry_Pi1.GPIO27, U1.IN1
  N4: Raspberry_Pi1.GPIO22, U1.IN2
  N5: Raspberry_Pi1.GPIO5, J1.pulse
  N6: Raspberry_Pi1.GPIO6, Part1.Trig
  N7: Raspberry_Pi1.GPIO13, Part1.Echo
  N8: Raspberry_Pi1.GPIO25, U1.IN4
  N9: Raspberry_Pi1.GPIO24, U1.IN3
  N10: Raspberry_Pi1.GPIO23, U1.ENB
  5V: Raspberry_Pi1.5V, U1.VLS, Part1.VCC, PIR1.VDD
  N11: U1.OUT1, Right_Front.pin_1, Right_Rear.pin_1
  N12: U1.OUT2, Right_Front.pin_2, Right_Rear.pin_2
  N13: U1.VS, J1.vcc, VCC1.+
  GND_2: U1.GND, J1.gnd, VCC1.-
  N14: U1.OUT3, Left_Front.pin_1, Left_Rear.pin_1
  N15: U1.OUT4, Left_Front.pin_2, Left_Rear.pin_2

custom parts:
  Battery: Your standard 2x 18650 battery pack (7,4 Volts)
